// Logisim project EXMEM.circ as structural Verilog: 1 circuit, main circuit main
module main (
  input  clk,
  input  branch,
  input  mem_read,
  input  mem_write,
  input  reg_write,
  input  mem_to_reg,
  input  [23:0] BRANCH_add,
  input  ZERO,
  input  [31:0] ALU_RES,
  input  [31:0] data_2,
  input  [4:0] RD,
  output branch_2,
  output mem_read_2,
  output mem_write_2,
  output reg_write_2,
  output mem_to_reg_2,
  output [23:0] branch_address,
  output zero_flag,
  output [31:0] ALU_RES_2,
  output [31:0] data2,
  output [4:0] RD_2
);

  Register #(.width(1)) u_branch (.D(branch), .Q(branch_2), .clk(clk));  // open: en, clr
  Register #(.width(1)) u_Mem_read (.D(mem_read), .Q(mem_read_2), .clk(clk));  // open: en, clr
  Register #(.width(1)) u_Mem_write (.D(mem_write), .Q(mem_write_2), .clk(clk));  // open: en, clr
  Register #(.width(1)) u_reg_write (.D(reg_write), .Q(reg_write_2), .clk(clk));  // open: en, clr
  Register #(.width(1)) u_mem_to_reg (.D(mem_to_reg), .Q(mem_to_reg_2), .clk(clk));  // open: en, clr
  Register #(.width(5)) u_RD (.D(RD), .Q(RD_2), .clk(clk));  // open: en, clr
  Register #(.width(24)) u_BRANCH_2 (.D(BRANCH_add), .Q(branch_address), .clk(clk));  // open: en, clr
  Register #(.width(1)) u_ZERO (.D(ZERO), .Q(zero_flag), .clk(clk));  // open: en, clr
  Register #(.width(32)) u_ALU_RES (.D(ALU_RES), .Q(ALU_RES_2), .clk(clk));  // open: en, clr
  Register #(.width(32)) RT (.D(data_2), .Q(data2), .clk(clk));  // open: en, clr
endmodule
