// Logisim project IDEX.circ as structural Verilog: 1 circuit, main circuit main
module main (
  input  [23:0] PC,
  input  [31:0] DATA_1,
  input  [31:0] DATA_2,
  input  [31:0] IMM,
  input  [4:0] RT,
  input  [4:0] RD,
  input  clk,
  input  Aluop1,
  input  AluOp2,
  input  Alu_src,
  input  Reg_Dest,
  input  branch,
  input  mem_read,
  input  mem_write,
  input  mem_to_reg,
  input  reg_write,
  input  [2:0] alu_con,
  output [23:0] pc_updated,
  output [31:0] DATA_1_2,
  output [31:0] DATA_2_2,
  output [31:0] imm_2,
  output [4:0] RT_2,
  output [4:0] RD_2,
  output alu_op1,
  output alu_op2,
  output Alu_src_2,
  output Reg_Dest_2,
  output branch_2,
  output mem_read_2,
  output mem_write_2,
  output mem_to_reg_2,
  output reg_write_2,
  output [2:0] alu_con_2
);

  Register #(.width(1)) u_branch (.D(branch), .Q(branch_2), .clk(clk));  // open: en, clr
  Register #(.width(1)) u_Mem_Read (.D(mem_read), .Q(mem_read_2), .clk(clk));  // open: en, clr
  Register #(.width(3)) register_1 (.D(alu_con), .Q(alu_con_2), .clk(clk));  // open: en, clr
  Register #(.width(24)) u_PC (.D(PC), .Q(pc_updated), .clk(clk));  // open: en, clr
  Register #(.width(32)) u_DATA_1 (.D(DATA_1), .Q(DATA_1_2), .clk(clk));  // open: en, clr
  Register #(.width(32)) u_DATA_2 (.D(DATA_2), .Q(DATA_2_2), .clk(clk));  // open: en, clr
  Register #(.width(32)) u_IMM (.D(IMM), .Q(imm_2), .clk(clk));  // open: en, clr
  Register #(.width(5)) u_RT (.D(RT), .Q(RT_2), .clk(clk));  // open: en, clr
  Register #(.width(5)) u_RD (.D(RD), .Q(RD_2), .clk(clk));  // open: en, clr
  Register #(.width(1)) u_AluOp1 (.D(Aluop1), .Q(alu_op1), .clk(clk));  // open: en, clr
  Register #(.width(1)) u_AluOp2 (.D(AluOp2), .Q(alu_op2), .clk(clk));  // open: en, clr
  Register #(.width(1)) u_mem_to_reg (.D(mem_to_reg), .Q(mem_to_reg_2), .clk(clk));  // open: en, clr
  Register #(.width(1)) u_reg_write (.D(reg_write), .Q(reg_write_2), .clk(clk));  // open: en, clr
  Register #(.width(1)) AluSrc (.D(Alu_src), .Q(Alu_src_2), .clk(clk));  // open: en, clr
  Register #(.width(1)) RegDest (.D(Reg_Dest), .Q(Reg_Dest_2), .clk(clk));  // open: en, clr
  Register #(.width(1)) MemWrite (.D(mem_write), .Q(mem_write_2), .clk(clk));  // open: en, clr
endmodule
