// Logisim project IFID.circ as structural Verilog: 1 circuit, main circuit main
module main (
  input  [31:0] Instruction,
  input  [23:0] PC_Updated,
  input  clk,
  output [31:0] ins,
  output [23:0] PC_Updated_2
);

  Register #(.width(32)) u_INS (.D(Instruction), .Q(ins), .clk(clk));  // open: en, clr
  Register #(.width(24)) PC (.D(PC_Updated), .Q(PC_Updated_2), .clk(clk));  // open: en, clr
endmodule
