// Logisim project MEMWB.circ as structural Verilog: 1 circuit, main circuit main
module main (
  input  [31:0] ALU_RES,
  input  [31:0] memory_word,
  input  [4:0] rd,
  input  reg_write,
  input  mem_to_reg,
  input  clk,
  output [31:0] alu_result,
  output [31:0] memory_word_2,
  output [4:0] rd_2,
  output reg_write_2,
  output mem_to_reg_2
);

  Register #(.width(32)) u_alu_result (.D(ALU_RES), .Q(alu_result), .clk(clk));  // open: en, clr
  Register #(.width(32)) memoryword (.D(memory_word), .Q(memory_word_2), .clk(clk));  // open: en, clr
  Register #(.width(5)) u_rd (.D(rd), .Q(rd_2), .clk(clk));  // open: en, clr
  Register #(.width(1)) u_reg_write (.D(reg_write), .Q(reg_write_2), .clk(clk));  // open: en, clr
  Register #(.width(1)) u_mem_to_reg (.D(mem_to_reg), .Q(mem_to_reg_2), .clk(clk));  // open: en, clr
endmodule
