// Logisim project alu control (team 25).circ as structural Verilog: 1 circuit, main circuit main
module main (
  input  fun5,
  input  fun4,
  input  fun3,
  input  fun2,
  input  fun1,
  input  fun0,
  input  alu_op2,
  input  alu_op1,
  output alu_op2_2,
  output alu_op1_2,
  output alu_op0
);

  wire add_out, and_out, beq_out, lw_sw_out, not_1_out, not_2_out, not_3_out, not_4_out, not_5_out,
       not_6_out, not_7_out, not_8_out, or_out, slt_out, sub_out;

  not not_1 (not_1_out, fun5);
  not not_2 (not_2_out, fun4);
  not not_3 (not_3_out, fun3);
  not not_4 (not_4_out, fun2);
  not not_5 (not_5_out, fun1);
  not not_6 (not_6_out, fun0);
  not not_7 (not_7_out, alu_op2);
  not not_8 (not_8_out, alu_op1);
  and lw_sw (lw_sw_out, not_8_out, not_7_out);
  and beq (beq_out, alu_op1, not_7_out);
  and add (add_out, not_8_out, alu_op2, fun5, not_2_out, not_3_out, not_4_out, not_5_out, not_6_out);
  and sub (sub_out, not_8_out, alu_op2, not_4_out, not_3_out, not_2_out, fun5, fun1, not_6_out);
  and \and  (and_out, fun5, not_2_out, not_3_out, fun2, not_5_out, not_6_out, not_8_out, alu_op2);
  and \or  (or_out, fun5, not_2_out, not_3_out, fun2, not_5_out, fun0, not_8_out, alu_op2);
  and slt (slt_out, fun5, not_2_out, fun3, not_4_out, fun1, not_6_out, not_8_out, alu_op2);
  or or_2 (alu_op2_2, beq_out, sub_out, slt_out);
  or or_3 (alu_op1_2, lw_sw_out, beq_out, add_out, sub_out, slt_out);
  or or_4 (alu_op0, or_out, slt_out);
endmodule
