// Logisim project alu.circ as structural Verilog: 1 circuit, main circuit main
module main (
  input  in_1,
  input  [31:0] op1,
  input  in_3,
  input  [31:0] op2,
  input  [2:0] aluOP,
  output out_6,
  output out_7,
  output [31:0] \output ,
  output out_9,
  output zero_flag
);

  wire comparator_1_lt;
  wire [31:0] adder_1_out, and_out, bit_extender_1_out, or_out, subtractor_1_out;

  Adder #(.width(32)) adder_1 (.a(op1), .b(op2), .out(adder_1_out), .cin(in_1), .cout(out_6));
  Subtractor #(.width(32)) subtractor_1 (.a(op1), .b(op2), .out(subtractor_1_out), .bin(in_3), .bout(out_7));
  assign or_out = op1 | op2;  // OR_Gate or, 32 bits wide
  assign and_out = op1 & op2;  // AND_Gate and, 32 bits wide
  Comparator #(.width(32)) comparator_1 (.a(op1), .b(op2), .gt(out_9), .eq(zero_flag), .lt(comparator_1_lt));
  assign bit_extender_1_out = {{31{1'b0}}, comparator_1_lt};  // Bit_Extender bit_extender_1
  Multiplexer #(.select(3), .width(32), .enable("false")) multiplexer_1 (
    .in0(adder_1_out), .in1(subtractor_1_out), .in5(or_out), .in6(and_out), .in7(bit_extender_1_out),
    .out(\output ), .sel(aluOP));  // open: in2, in3, in4
endmodule
