// Logisim project control unit (Team 25).circ as structural Verilog: 1 circuit, main circuit main
module main (
  input  _26__A,
  input  _27__B,
  input  _28__C,
  input  _29__D,
  input  _30__E,
  input  _31__F,
  output RegDest,
  output alu_op2,
  output aluop1,
  output Branch,
  output Reg_Write,
  output Mem_Read,
  output Mem_To_Reg,
  output Mem_write,
  output ALU_src
);

  and r_format (alu_op2, ~_26__A, ~_27__B, ~_28__C, ~_29__D, ~_30__E, ~_31__F);  // AND_Gate
  and beq (aluop1, ~_26__A, ~_27__B, _28__C, ~_29__D, ~_30__E, ~_31__F);  // AND_Gate
  and lw (Mem_Read, _26__A, _27__B, ~_28__C, ~_29__D, ~_30__E, _31__F);  // AND_Gate
  and sw (Mem_write, _26__A, _27__B, ~_28__C, _29__D, ~_30__E, _31__F);  // AND_Gate
  or or_1 (Reg_Write, alu_op2, Mem_Read);
  or or_2 (ALU_src, Mem_Read, Mem_write);

  assign Branch = aluop1;
  assign Mem_To_Reg = Mem_Read;
  assign RegDest = alu_op2;
endmodule
