// Logisim project datapath.circ as structural Verilog: 9 circuits, main circuit main
// EX/MEM
module main (
);

  wire ALU_Src, ALU_Src1, ALUOP1, aluOp1_t, ALUOP2, aluOp2_t, and_1_out, Branch, Branch1, Branch2, clk,
       Mem_Read, Mem_Read1, Mem_Read2, Mem_to_Reg, Mem_to_Reg1, Mem_to_Reg2, Mem_to_Reg3, Mem_Write,
       Mem_Write1, Mem_Write2, Reg_Des, Reg_Dest, RegWr, RegWr1, RegWr2, RegWrite, ZeroF, ZeroFlag;
  wire [2:0] ALU_Con, alu_con1;
  wire [4:0] _11_15, _16_20, _21_25, rd2, rt2, Write_Reg, Write_Reg1, Write_Reg2;
  wire [5:0] _26_31;
  wire [10:0] _0_10;
  wire [23:0] bit_extender_4_out, bit_extender_5_out, branch_add, branch_address, PC, pc_1, pc_updated, pcIn,
       pcUP;
  wire [31:0] alu_res, alu_res1, alu_res2, bit_extender_1_out, data2, data2a, data_1, data_1a, forstore1,
       imm, imm_a, INS, mem_word, mem_word1, \output , PC_q, writeD;

  assign bit_extender_1_out = {{8{1'b0}}, pcIn};  // Bit_Extender bit_extender_1
  Bit_Extender #(.in_width(32), .out_width(24)) bit_extender_2 (.in(PC_q), .out(PC));
  Register #(.width(32)) u_PC (.D(bit_extender_1_out), .Q(PC_q), .clk(clk));  // open: en, clr
  IF_ID IF_ID (
    .Instruction(INS), .PC_Updated(pc_1), .clk(clk), .ins({_26_31, _21_25, _16_20, _11_15, _0_10}),
    .PC_Updated_2(pc_updated));
  alu_control alu_control (
    .fun5(_0_10[5]), .fun4(_0_10[4]), .fun3(_0_10[3]), .fun2(_0_10[2]), .fun1(_0_10[1]), .fun0(_0_10[0]),
    .alu_op2(ALUOP2), .alu_op1(ALUOP1), .alu_op2_2(ALU_Con[2]), .alu_op1_2(ALU_Con[1]), .alu_op0(ALU_Con[0]));
  Adder #(.width(24)) adder_1 (.a(PC), .b(24'h1), .out(pc_1));  // open: cin, cout
  RAM #(.addrWidth(24), .dataWidth(32)) ram_1 (.addr(PC), .data(INS), .clk(clk), .ld(1'b1));  // open: sel, clr
  assign imm = {{16{1'b0}}, {_11_15, _0_10}};  // Bit_Extender bit_extender_3
  Register_File RegFile (
    .WriteData(writeD), .clk(clk), .RegWrite(RegWr2), .ReadRegister2(_16_20), .ReadRegister1(_21_25),
    .ReadData2(data2), .ReadData1(data_1), .WriteRegister(Write_Reg2));
  Multiplexer #(.width(5), .enable("false")) multiplexer_1 (.in0(rt2), .in1(rd2), .out(Write_Reg), .sel(Reg_Dest));
  Multiplexer #(.width(32), .enable("false")) multiplexer_2 (.in0(data2a), .in1(imm_a), .out(\output ), .sel(ALU_Src1));
  Control_Unit control_unit_1 (
    ._26__A(_26_31[0]), ._27__B(_26_31[1]), ._28__C(_26_31[2]), ._29__D(_26_31[3]), ._30__E(_26_31[4]),
    ._31__F(_26_31[5]), .RegDest(Reg_Des), .alu_op2(aluOp2_t), .aluop1(aluOp1_t), .Branch(Branch),
    .Reg_Write(RegWrite), .Mem_Read(Mem_Read), .Mem_To_Reg(Mem_to_Reg), .Mem_write(Mem_Write),
    .ALU_src(ALU_Src));
  Bit_Extender #(.in_width(32), .out_width(24)) bit_extender_4 (.in(imm_a), .out(bit_extender_4_out));
  Adder #(.width(24)) adder_2 (.a(bit_extender_4_out), .b(pcUP), .out(branch_address));  // open: cin, cout
  ALU ALU (
    .op1(data_1a), .op2(\output ), .aluOP(alu_con1), .\output (alu_res), .zero_flag(ZeroF));  // open: in_1, out_6, out_7, in_3, less_than
  ID_EX ID_EX (
    .PC(pc_updated), .DATA_1(data_1), .DATA_2(data2), .IMM(imm), .RT(_16_20), .RD(_11_15), .clk(clk),
    .Aluop1(aluOp1_t), .AluOp2(aluOp2_t), .Alu_src(ALU_Src), .Reg_Dest(Reg_Des), .branch(Branch),
    .mem_read(Mem_Read), .mem_write(Mem_Write), .mem_to_reg(Mem_to_Reg), .reg_write(RegWrite),
    .alu_con(ALU_Con), .pc_updated(pcUP), .DATA_1_2(data_1a), .DATA_2_2(data2a), .imm_2(imm_a), .RT_2(rt2),
    .RD_2(rd2), .alu_op1(ALUOP1), .alu_op2(ALUOP2), .Alu_src_2(ALU_Src1), .Reg_Dest_2(Reg_Dest),
    .branch_2(Branch1), .mem_read_2(Mem_Read1), .mem_write_2(Mem_Write1), .mem_to_reg_2(Mem_to_Reg1),
    .reg_write_2(RegWr), .alu_con_2(alu_con1));
  Bit_Extender #(.in_width(32), .out_width(24)) bit_extender_5 (.in(alu_res1), .out(bit_extender_5_out));
  Multiplexer #(.width(24), .enable("false")) multiplexer_3 (.in0(pc_1), .in1(branch_add), .out(pcIn), .sel(and_1_out));
  and and_1 (and_1_out, Branch2, ZeroFlag);
  EX_MEM EX_MEM (
    .clk(clk), .branch(Branch1), .mem_read(Mem_Read1), .mem_write(Mem_Write1), .reg_write(RegWr),
    .mem_to_reg(Mem_to_Reg1), .BRANCH_add(branch_address), .ZERO(ZeroF), .ALU_RES(alu_res), .data_2(data2a),
    .RD(Write_Reg), .branch_2(Branch2), .mem_read_2(Mem_Read2), .mem_write_2(Mem_Write2),
    .reg_write_2(RegWr1), .mem_to_reg_2(Mem_to_Reg2), .branch_address(branch_add), .zero_flag(ZeroFlag),
    .ALU_RES_2(alu_res1), .data2(forstore1), .RD_2(Write_Reg1));
  Clock clock_1 (.out(clk));
  RAM #(.addrWidth(24), .dataWidth(32), .bus("separate")) ram_2 (
    .addr(bit_extender_5_out), .din(forstore1), .data(mem_word), .str(Mem_Write2), .clk(clk), .ld(Mem_Read2));  // open: sel, clr
  MEM_WB MEM_WB (
    .ALU_RES(alu_res1), .memory_word(mem_word), .rd(Write_Reg1), .reg_write(RegWr1),
    .mem_to_reg(Mem_to_Reg2), .clk(clk), .alu_result(alu_res2), .memory_word_2(mem_word1), .rd_2(Write_Reg2),
    .reg_write_2(RegWr2), .mem_to_reg_2(Mem_to_Reg3));
  Multiplexer #(.width(32), .enable("false")) multiplexer_4 (
    .in0(alu_res2), .in1(mem_word1), .out(writeD), .sel(Mem_to_Reg3));

  // Other names for the same wires on the sheet: func[5:0] = _0_10[5:0];
  //   INS1[31:0] = {_26_31, _21_25, _16_20, _11_15, _0_10}; rd[4:0] = _11_15; alu_res1a[31:0] = alu_res1;
  //   forstore[31:0] = data2a; imm_a1[31:0] = imm_a; output1[31:0] = \output ; pc_inc[23:0] = pc_1;
  //   pcUP1[23:0] = pcUP; rt[4:0] = _16_20
endmodule

module ALU (
  input  in_1,
  input  [31:0] op1,
  input  in_3,
  input  [31:0] op2,
  input  [2:0] aluOP,
  output out_6,
  output out_7,
  output [31:0] \output ,
  output less_than,
  output zero_flag
);

  wire comparator_1_lt;
  wire [31:0] add, \and , \or , slt, sub;

  Adder #(.width(32)) adder_1 (.a(op1), .b(op2), .out(add), .cin(in_1), .cout(out_6));
  Subtractor #(.width(32)) subtractor_1 (.a(op1), .b(op2), .out(sub), .bin(in_3), .bout(out_7));
  assign \or  = op1 | op2;  // OR_Gate or, 32 bits wide
  assign \and  = op1 & op2;  // AND_Gate and, 32 bits wide
  Comparator #(.width(32)) comparator_1 (.a(op1), .b(op2), .gt(less_than), .eq(zero_flag), .lt(comparator_1_lt));
  assign slt = {{31{1'b0}}, comparator_1_lt};  // Bit_Extender bit_extender_1
  Multiplexer #(.select(3), .width(32), .enable("false")) multiplexer_1 (
    .in0(\and ), .in1(\or ), .in2(add), .in6(sub), .in7(slt), .out(\output ), .sel(aluOP));  // open: in3, in4, in5
endmodule

module Register_File (
  input  [31:0] WriteData,
  input  clk,
  input  RegWrite,
  input  [4:0] WriteRegister,
  input  [4:0] ReadRegister2,
  input  [4:0] ReadRegister1,
  output [31:0] ReadData2,
  output [31:0] ReadData1
);

  wire _0, _1, _2, _3, _4, _5, _6, _7, _8, _9, _10, _11, _12, _13, _14, _15, _16, _17, _18, _19, _20, _21,
       _22, _23, _24, _25, _26, _27, _28, _29, _30, _31;
  wire [31:0] r0, r1, r2, r3, r4, r5, r6, r7, r8, r9, r10, r11, r12, r13, r14, r15, r16, r17, r18, r19, r20,
       r21, r22, r23, r24, r25, r26, r27, r28, r29, r30, r31;

  Decoder #(.select(5), .disabled(0)) decoder_1 (
    .out0(_0), .out1(_1), .out2(_2), .out3(_3), .out4(_4), .out5(_5), .out6(_6), .out7(_7), .out8(_8),
    .out9(_9), .out10(_10), .out11(_11), .out12(_12), .out13(_13), .out14(_14), .out15(_15), .out16(_16),
    .out17(_17), .out18(_18), .out19(_19), .out20(_20), .out21(_21), .out22(_22), .out23(_23), .out24(_24),
    .out25(_25), .out26(_26), .out27(_27), .out28(_28), .out29(_29), .out30(_30), .out31(_31),
    .sel(WriteRegister), .en(RegWrite));
  Register #(.width(32)) register_1 (.D({32{1'b0}}), .en(_0), .Q(r0), .clk(clk));  // open: clr
  Register #(.width(32)) register_2 (.D(WriteData), .en(_9), .Q(r9), .clk(clk));  // open: clr
  Register #(.width(32)) register_3 (.D(WriteData), .en(_21), .Q(r21), .clk(clk));  // open: clr
  Register #(.width(32)) register_4 (.D(WriteData), .en(_1), .Q(r1), .clk(clk));  // open: clr
  Register #(.width(32)) register_5 (.D(WriteData), .en(_10), .Q(r10), .clk(clk));  // open: clr
  Register #(.width(32)) register_6 (.D(WriteData), .en(_22), .Q(r22), .clk(clk));  // open: clr
  Register #(.width(32)) register_7 (.D(WriteData), .en(_11), .Q(r11), .clk(clk));  // open: clr
  Register #(.width(32)) register_8 (.D(WriteData), .en(_2), .Q(r2), .clk(clk));  // open: clr
  Register #(.width(32)) register_9 (.D(WriteData), .en(_23), .Q(r23), .clk(clk));  // open: clr
  Register #(.width(32)) register_10 (.D(WriteData), .en(_3), .Q(r3), .clk(clk));  // open: clr
  Register #(.width(32)) register_11 (.D(WriteData), .en(_12), .Q(r12), .clk(clk));  // open: clr
  Register #(.width(32)) register_12 (.D(WriteData), .en(_24), .Q(r24), .clk(clk));  // open: clr
  Register #(.width(32)) register_13 (.D(WriteData), .en(_4), .Q(r4), .clk(clk));  // open: clr
  Register #(.width(32)) register_14 (.D(WriteData), .en(_13), .Q(r13), .clk(clk));  // open: clr
  Register #(.width(32)) register_15 (.D(WriteData), .en(_25), .Q(r25), .clk(clk));  // open: clr
  Register #(.width(32)) register_16 (.D(WriteData), .en(_5), .Q(r5), .clk(clk));  // open: clr
  Register #(.width(32)) register_17 (.D(WriteData), .en(_14), .Q(r14), .clk(clk));  // open: clr
  Register #(.width(32)) register_18 (.D(WriteData), .en(_26), .Q(r26), .clk(clk));  // open: clr
  Multiplexer #(.select(5), .width(32), .enable("false")) multiplexer_1 (
    .in0(r0), .in1(r1), .in2(r2), .in3(r3), .in4(r4), .in5(r5), .in6(r6), .in7(r7), .in8(r8), .in9(r9),
    .in10(r10), .in11(r11), .in12(r12), .in13(r13), .in14(r14), .in15(r15), .in16(r16), .in17(r17),
    .in18(r18), .in19(r19), .in20(r20), .in21(r21), .in22(r22), .in23(r23), .in24(r24), .in25(r25),
    .in26(r26), .in27(r27), .in28(r28), .in29(r29), .in30(r30), .in31(r31), .out(ReadData2),
    .sel(ReadRegister2));
  Register #(.width(32)) register_19 (.D(WriteData), .en(_15), .Q(r15), .clk(clk));  // open: clr
  Register #(.width(32)) register_20 (.D(WriteData), .en(_6), .Q(r6), .clk(clk));  // open: clr
  Register #(.width(32)) register_21 (.D(WriteData), .en(_16), .Q(r16), .clk(clk));  // open: clr
  Register #(.width(32)) register_22 (.D(WriteData), .en(_27), .Q(r27), .clk(clk));  // open: clr
  Register #(.width(32)) register_23 (.D(WriteData), .en(_7), .Q(r7), .clk(clk));  // open: clr
  Register #(.width(32)) register_24 (.D(WriteData), .en(_17), .Q(r17), .clk(clk));  // open: clr
  Register #(.width(32)) register_25 (.D(WriteData), .en(_28), .Q(r28), .clk(clk));  // open: clr
  Multiplexer #(.select(5), .width(32), .enable("false")) multiplexer_2 (
    .in0(r0), .in1(r1), .in2(r2), .in3(r3), .in4(r4), .in5(r5), .in6(r6), .in7(r7), .in8(r8), .in9(r9),
    .in10(r10), .in11(r11), .in12(r12), .in13(r13), .in14(r14), .in15(r15), .in16(r16), .in17(r17),
    .in18(r18), .in19(r19), .in20(r20), .in21(r21), .in22(r22), .in23(r23), .in24(r24), .in25(r25),
    .in26(r26), .in27(r27), .in28(r28), .in29(r29), .in30(r30), .in31(r31), .out(ReadData1),
    .sel(ReadRegister1));
  Register #(.width(32)) register_26 (.D(WriteData), .en(_18), .Q(r18), .clk(clk));  // open: clr
  Register #(.width(32)) register_27 (.D(WriteData), .en(_29), .Q(r29), .clk(clk));  // open: clr
  Register #(.width(32)) register_28 (.D(WriteData), .en(_8), .Q(r8), .clk(clk));  // open: clr
  Register #(.width(32)) register_29 (.D(WriteData), .en(_30), .Q(r30), .clk(clk));  // open: clr
  Register #(.width(32)) register_30 (.D(WriteData), .en(_19), .Q(r19), .clk(clk));  // open: clr
  Register #(.width(32)) register_31 (.D(WriteData), .en(_20), .Q(r20), .clk(clk));  // open: clr
  Register #(.width(32)) register_32 (.D(WriteData), .en(_31), .Q(r31), .clk(clk));  // open: clr

  // Other names for the same wires on the sheet: c = clk; data[31:0] = WriteData
endmodule

// control unit
module Control_Unit (
  input  _26__A,
  input  _27__B,
  input  _28__C,
  input  _29__D,
  input  _30__E,
  input  _31__F,
  output RegDest,
  output alu_op2,
  output aluop1,
  output Branch,
  output Reg_Write,
  output Mem_Read,
  output Mem_To_Reg,
  output Mem_write,
  output ALU_src
);

  and r_format (alu_op2, ~_26__A, ~_27__B, ~_28__C, ~_29__D, ~_30__E, ~_31__F);  // AND_Gate
  and beq (aluop1, ~_26__A, ~_27__B, _28__C, ~_29__D, ~_30__E, ~_31__F);  // AND_Gate
  and lw (Mem_Read, _26__A, _27__B, ~_28__C, ~_29__D, ~_30__E, _31__F);  // AND_Gate
  and sw (Mem_write, _26__A, _27__B, ~_28__C, _29__D, ~_30__E, _31__F);  // AND_Gate
  or or_1 (Reg_Write, alu_op2, Mem_Read);
  or or_2 (ALU_src, Mem_Read, Mem_write);

  assign Branch = aluop1;
  assign Mem_To_Reg = Mem_Read;
  assign RegDest = alu_op2;
endmodule

module IF_ID (
  input  [31:0] Instruction,
  input  [23:0] PC_Updated,
  input  clk,
  output [31:0] ins,
  output [23:0] PC_Updated_2
);

  Register #(.width(32)) u_INS (.D(Instruction), .Q(ins), .clk(clk));  // open: en, clr
  Register #(.width(24)) PC (.D(PC_Updated), .Q(PC_Updated_2), .clk(clk));  // open: en, clr
endmodule

module ID_EX (
  input  [23:0] PC,
  input  [31:0] DATA_1,
  input  [31:0] DATA_2,
  input  [31:0] IMM,
  input  [4:0] RT,
  input  [4:0] RD,
  input  clk,
  input  Aluop1,
  input  AluOp2,
  input  Alu_src,
  input  Reg_Dest,
  input  branch,
  input  mem_read,
  input  mem_write,
  input  mem_to_reg,
  input  reg_write,
  input  [2:0] alu_con,
  output [23:0] pc_updated,
  output [31:0] DATA_1_2,
  output [31:0] DATA_2_2,
  output [31:0] imm_2,
  output [4:0] RT_2,
  output [4:0] RD_2,
  output alu_op1,
  output alu_op2,
  output Alu_src_2,
  output Reg_Dest_2,
  output branch_2,
  output mem_read_2,
  output mem_write_2,
  output mem_to_reg_2,
  output reg_write_2,
  output [2:0] alu_con_2
);

  Register #(.width(1)) u_branch (.D(branch), .Q(branch_2), .clk(clk));  // open: en, clr
  Register #(.width(1)) u_Mem_Read (.D(mem_read), .Q(mem_read_2), .clk(clk));  // open: en, clr
  Register #(.width(3)) register_1 (.D(alu_con), .Q(alu_con_2), .clk(clk));  // open: en, clr
  Register #(.width(24)) u_PC (.D(PC), .Q(pc_updated), .clk(clk));  // open: en, clr
  Register #(.width(32)) u_DATA_1 (.D(DATA_1), .Q(DATA_1_2), .clk(clk));  // open: en, clr
  Register #(.width(32)) u_DATA_2 (.D(DATA_2), .Q(DATA_2_2), .clk(clk));  // open: en, clr
  Register #(.width(32)) u_IMM (.D(IMM), .Q(imm_2), .clk(clk));  // open: en, clr
  Register #(.width(5)) u_RT (.D(RT), .Q(RT_2), .clk(clk));  // open: en, clr
  Register #(.width(5)) u_RD (.D(RD), .Q(RD_2), .clk(clk));  // open: en, clr
  Register #(.width(1)) u_AluOp1 (.D(Aluop1), .Q(alu_op1), .clk(clk));  // open: en, clr
  Register #(.width(1)) u_AluOp2 (.D(AluOp2), .Q(alu_op2), .clk(clk));  // open: en, clr
  Register #(.width(1)) u_mem_to_reg (.D(mem_to_reg), .Q(mem_to_reg_2), .clk(clk));  // open: en, clr
  Register #(.width(1)) u_reg_write (.D(reg_write), .Q(reg_write_2), .clk(clk));  // open: en, clr
  Register #(.width(1)) AluSrc (.D(Alu_src), .Q(Alu_src_2), .clk(clk));  // open: en, clr
  Register #(.width(1)) RegDest (.D(Reg_Dest), .Q(Reg_Dest_2), .clk(clk));  // open: en, clr
  Register #(.width(1)) MemWrite (.D(mem_write), .Q(mem_write_2), .clk(clk));  // open: en, clr
endmodule

module EX_MEM (
  input  clk,
  input  branch,
  input  mem_read,
  input  mem_write,
  input  reg_write,
  input  mem_to_reg,
  input  [23:0] BRANCH_add,
  input  ZERO,
  input  [31:0] ALU_RES,
  input  [31:0] data_2,
  input  [4:0] RD,
  output branch_2,
  output mem_read_2,
  output mem_write_2,
  output reg_write_2,
  output mem_to_reg_2,
  output [23:0] branch_address,
  output zero_flag,
  output [31:0] ALU_RES_2,
  output [31:0] data2,
  output [4:0] RD_2
);

  Register #(.width(1)) u_branch (.D(branch), .Q(branch_2), .clk(clk));  // open: en, clr
  Register #(.width(1)) u_Mem_read (.D(mem_read), .Q(mem_read_2), .clk(clk));  // open: en, clr
  Register #(.width(1)) u_Mem_write (.D(mem_write), .Q(mem_write_2), .clk(clk));  // open: en, clr
  Register #(.width(1)) u_reg_write (.D(reg_write), .Q(reg_write_2), .clk(clk));  // open: en, clr
  Register #(.width(1)) u_mem_to_reg (.D(mem_to_reg), .Q(mem_to_reg_2), .clk(clk));  // open: en, clr
  Register #(.width(5)) u_RD (.D(RD), .Q(RD_2), .clk(clk));  // open: en, clr
  Register #(.width(24)) u_BRANCH_2 (.D(BRANCH_add), .Q(branch_address), .clk(clk));  // open: en, clr
  Register #(.width(1)) u_ZERO (.D(ZERO), .Q(zero_flag), .clk(clk));  // open: en, clr
  Register #(.width(32)) u_ALU_RES (.D(ALU_RES), .Q(ALU_RES_2), .clk(clk));  // open: en, clr
  Register #(.width(32)) RT (.D(data_2), .Q(data2), .clk(clk));  // open: en, clr
endmodule

module MEM_WB (
  input  [31:0] ALU_RES,
  input  [31:0] memory_word,
  input  [4:0] rd,
  input  reg_write,
  input  mem_to_reg,
  input  clk,
  output [31:0] alu_result,
  output [31:0] memory_word_2,
  output [4:0] rd_2,
  output reg_write_2,
  output mem_to_reg_2
);

  Register #(.width(32)) u_alu_result (.D(ALU_RES), .Q(alu_result), .clk(clk));  // open: en, clr
  Register #(.width(32)) memoryword (.D(memory_word), .Q(memory_word_2), .clk(clk));  // open: en, clr
  Register #(.width(5)) u_rd (.D(rd), .Q(rd_2), .clk(clk));  // open: en, clr
  Register #(.width(1)) u_reg_write (.D(reg_write), .Q(reg_write_2), .clk(clk));  // open: en, clr
  Register #(.width(1)) u_mem_to_reg (.D(mem_to_reg), .Q(mem_to_reg_2), .clk(clk));  // open: en, clr
endmodule

module alu_control (
  input  fun5,
  input  fun4,
  input  fun3,
  input  fun2,
  input  fun1,
  input  fun0,
  input  alu_op2,
  input  alu_op1,
  output alu_op2_2,
  output alu_op1_2,
  output alu_op0
);

  wire add_out, and_out, beq_out, lw_sw_out, not_1_out, not_2_out, not_3_out, not_4_out, not_5_out,
       not_6_out, not_7_out, not_8_out, or_out, slt_out, sub_out;

  not not_1 (not_1_out, fun5);
  not not_2 (not_2_out, fun4);
  not not_3 (not_3_out, fun3);
  not not_4 (not_4_out, fun2);
  not not_5 (not_5_out, fun1);
  not not_6 (not_6_out, fun0);
  not not_7 (not_7_out, alu_op2);
  not not_8 (not_8_out, alu_op1);
  and lw_sw (lw_sw_out, not_8_out, not_7_out);
  and beq (beq_out, alu_op1, not_7_out);
  and add (add_out, not_8_out, alu_op2, fun5, not_2_out, not_3_out, not_4_out, not_5_out, not_6_out);
  and sub (sub_out, not_8_out, alu_op2, not_4_out, not_3_out, not_2_out, fun5, fun1, not_6_out);
  and \and  (and_out, fun5, not_2_out, not_3_out, fun2, not_5_out, not_6_out, not_8_out, alu_op2);
  and \or  (or_out, fun5, not_2_out, not_3_out, fun2, not_5_out, fun0, not_8_out, alu_op2);
  and slt (slt_out, fun5, not_2_out, fun3, not_4_out, fun1, not_6_out, not_8_out, alu_op2);
  or or_2 (alu_op2_2, beq_out, sub_out, slt_out);
  or or_3 (alu_op1_2, lw_sw_out, beq_out, add_out, sub_out, slt_out);
  or or_4 (alu_op0, or_out, slt_out);
endmodule
