// Logisim project resgister-file.circ as structural Verilog: 1 circuit, main circuit main
module main (
  input  [31:0] WriteData,
  input  clk,
  input  RegWrite,
  input  [4:0] WriteRegister,
  input  [4:0] ReadRegister2,
  input  [4:0] ReadRegister1,
  output [31:0] ReadData2,
  output [31:0] ReadData1
);

  wire _0, _1, _2, _3, _4, _5, _6, _7, _8, _9, _10, _11, _12, _13, _14, _15, _16, _17, _18, _19, _20, _21,
       _22, _23, _24, _25, _26, _27, _28, _29, _30, _31;
  wire [31:0] r0, r1, r2, r3, r4, r5, r6, r7, r8, r9, r10, r11, r12, r13, r14, r15, r16, r17, r18, r19, r20,
       r21, r22, r23, r24, r25, r26, r27, r28, r29, r30, r31;

  Decoder #(.select(5), .disabled(0)) decoder_1 (
    .out0(_0), .out1(_1), .out2(_2), .out3(_3), .out4(_4), .out5(_5), .out6(_6), .out7(_7), .out8(_8),
    .out9(_9), .out10(_10), .out11(_11), .out12(_12), .out13(_13), .out14(_14), .out15(_15), .out16(_16),
    .out17(_17), .out18(_18), .out19(_19), .out20(_20), .out21(_21), .out22(_22), .out23(_23), .out24(_24),
    .out25(_25), .out26(_26), .out27(_27), .out28(_28), .out29(_29), .out30(_30), .out31(_31),
    .sel(WriteRegister), .en(RegWrite));
  Register #(.width(32)) register_1 (.D({32{1'b0}}), .en(_0), .Q(r0), .clk(clk));  // open: clr
  Register #(.width(32)) register_2 (.D(WriteData), .en(_9), .Q(r9), .clk(clk));  // open: clr
  Register #(.width(32)) register_3 (.D(WriteData), .en(_21), .Q(r21), .clk(clk));  // open: clr
  Register #(.width(32)) register_4 (.D(WriteData), .en(_1), .Q(r1), .clk(clk));  // open: clr
  Register #(.width(32)) register_5 (.D(WriteData), .en(_10), .Q(r10), .clk(clk));  // open: clr
  Register #(.width(32)) register_6 (.D(WriteData), .en(_22), .Q(r22), .clk(clk));  // open: clr
  Register #(.width(32)) register_7 (.D(WriteData), .en(_11), .Q(r11), .clk(clk));  // open: clr
  Register #(.width(32)) register_8 (.D(WriteData), .en(_2), .Q(r2), .clk(clk));  // open: clr
  Register #(.width(32)) register_9 (.D(WriteData), .en(_23), .Q(r23), .clk(clk));  // open: clr
  Register #(.width(32)) register_10 (.D(WriteData), .en(_3), .Q(r3), .clk(clk));  // open: clr
  Register #(.width(32)) register_11 (.D(WriteData), .en(_12), .Q(r12), .clk(clk));  // open: clr
  Register #(.width(32)) register_12 (.D(WriteData), .en(_24), .Q(r24), .clk(clk));  // open: clr
  Register #(.width(32)) register_13 (.D(WriteData), .en(_4), .Q(r4), .clk(clk));  // open: clr
  Register #(.width(32)) register_14 (.D(WriteData), .en(_13), .Q(r13), .clk(clk));  // open: clr
  Register #(.width(32)) register_15 (.D(WriteData), .en(_25), .Q(r25), .clk(clk));  // open: clr
  Register #(.width(32)) register_16 (.D(WriteData), .en(_5), .Q(r5), .clk(clk));  // open: clr
  Register #(.width(32)) register_17 (.D(WriteData), .en(_14), .Q(r14), .clk(clk));  // open: clr
  Register #(.width(32)) register_18 (.D(WriteData), .en(_26), .Q(r26), .clk(clk));  // open: clr
  Multiplexer #(.select(5), .width(32), .enable("false")) multiplexer_1 (
    .in0(r0), .in1(r1), .in2(r2), .in3(r3), .in4(r4), .in5(r5), .in6(r6), .in7(r7), .in8(r8), .in9(r9),
    .in10(r10), .in11(r11), .in12(r12), .in13(r13), .in14(r14), .in15(r15), .in16(r16), .in17(r17),
    .in18(r18), .in19(r19), .in20(r20), .in21(r21), .in22(r22), .in23(r23), .in24(r24), .in25(r25),
    .in26(r26), .in27(r27), .in28(r28), .in29(r29), .in30(r30), .in31(r31), .out(ReadData2),
    .sel(ReadRegister2));
  Register #(.width(32)) register_19 (.D(WriteData), .en(_15), .Q(r15), .clk(clk));  // open: clr
  Register #(.width(32)) register_20 (.D(WriteData), .en(_6), .Q(r6), .clk(clk));  // open: clr
  Register #(.width(32)) register_21 (.D(WriteData), .en(_16), .Q(r16), .clk(clk));  // open: clr
  Register #(.width(32)) register_22 (.D(WriteData), .en(_27), .Q(r27), .clk(clk));  // open: clr
  Register #(.width(32)) register_23 (.D(WriteData), .en(_7), .Q(r7), .clk(clk));  // open: clr
  Register #(.width(32)) register_24 (.D(WriteData), .en(_17), .Q(r17), .clk(clk));  // open: clr
  Register #(.width(32)) register_25 (.D(WriteData), .en(_28), .Q(r28), .clk(clk));  // open: clr
  Multiplexer #(.select(5), .width(32), .enable("false")) multiplexer_2 (
    .in0(r0), .in1(r1), .in2(r2), .in3(r3), .in4(r4), .in5(r5), .in6(r6), .in7(r7), .in8(r8), .in9(r9),
    .in10(r10), .in11(r11), .in12(r12), .in13(r13), .in14(r14), .in15(r15), .in16(r16), .in17(r17),
    .in18(r18), .in19(r19), .in20(r20), .in21(r21), .in22(r22), .in23(r23), .in24(r24), .in25(r25),
    .in26(r26), .in27(r27), .in28(r28), .in29(r29), .in30(r30), .in31(r31), .out(ReadData1),
    .sel(ReadRegister1));
  Register #(.width(32)) register_26 (.D(WriteData), .en(_18), .Q(r18), .clk(clk));  // open: clr
  Register #(.width(32)) register_27 (.D(WriteData), .en(_29), .Q(r29), .clk(clk));  // open: clr
  Register #(.width(32)) register_28 (.D(WriteData), .en(_8), .Q(r8), .clk(clk));  // open: clr
  Register #(.width(32)) register_29 (.D(WriteData), .en(_30), .Q(r30), .clk(clk));  // open: clr
  Register #(.width(32)) register_30 (.D(WriteData), .en(_19), .Q(r19), .clk(clk));  // open: clr
  Register #(.width(32)) register_31 (.D(WriteData), .en(_20), .Q(r20), .clk(clk));  // open: clr
  Register #(.width(32)) register_32 (.D(WriteData), .en(_31), .Q(r31), .clk(clk));  // open: clr

  // Other names for the same wires on the sheet: c = clk; data[31:0] = WriteData
endmodule
